# Fritzing sketch Master (saved by Fritzing 1.0.5)
breadboards: 3

parts:
  Mod2 = Amica NodeMCU DEVKIT 1.0
  Part1 = LCD1602-I2C  # not connected
  Sensor1 = Gas Sensor Breakout Board  # not connected
  microSD1 = MicroSD Card Module  # not connected
  GSM_SIM_GPSR_SMS_SIM900_SIM1 = SIM800L [package=THT]  # not connected
  RHT1 = Humidity and Temperature Sensor RHT03  # not connected
  A1 = PIR sensor (non-bendable legs)  # not connected
  S1 = Pushbutton [package="[THT]"]
  S2 = Pushbutton [package="[THT]"]
  LED1 = LED - 5mm [color="Red (633nm)" current=0.030A package="5 mm [THT]"]
  LED2 = LED - 5mm [color="Red (633nm)" current=0.030A package="5 mm [THT]"]
  R1 = Resistor [tolerance=±5% power=0.25W resistance=220 package=THT]
  R2 = Resistor [tolerance=±5% power=0.25W resistance=220 package=THT]

nets:
  N1: Mod2.pin1, Mod2.pin_10, Mod2.pin_26
  N2: Mod2.pin2, Mod2.pin_9, Mod2.pin_25, Mod2.pin_29
  N3: S1.Pin_1, S1.Pin_2
  N4: S1.Pin_3, S1.Pin_4, S2.Pin_3, S2.Pin_4, LED1.cathode, LED2.cathode
  N5: S2.Pin_1, S2.Pin_2
  N6: LED1.anode, R2.Pin_0
  N7: LED2.anode, R1.Pin_0

custom parts:
  LCD1602-I2C: A standard character display, usually with 2x16 characters. Comes in many colors with LCM1602 IIC attached.
  Gas Sensor Breakout Board: Gas sensor breakout board. Input voltage is 5V. Sensor output is available in analog and digital.
  PIR sensor (non-bendable legs): Generic PIR sensor
