# Fritzing sketch Water_Tank (saved by Fritzing 1.0.5)
breadboards: 2

parts:
  Mod1 = Amica NodeMCU DEVKIT 1.0
  Part1 = SRF05 Ultrasonic Rangefinder  # not connected

nets:
  N1: Mod1.pin1, Mod1.pin_10, Mod1.pin_26
  N2: Mod1.pin2, Mod1.pin_9, Mod1.pin_25, Mod1.pin_29
